// Logisim project ALU.circ as structural Verilog: 17 circuits, main circuit main
module main (
  input  [3:0] in_1,
  input  in_2,
  output [7:0] out_3,
  output [7:0] out_4,
  output [7:0] out_5,
  output [7:0] out_6
);

  wire n8bit_alu_1_cout, n8bit_alu_1_eq, n8bit_alu_1_gt, n8bit_alu_1_lt, n8bit_alu_1_zero;

  Register register_1 (.Q(out_3));  // open: D, en, clk, clr
  Register register_2 (.Q(out_4));  // open: D, en, clk, clr
  _8bit_ALU u_8bit_alu_1 (
    .in_1(out_3), .in_2(out_4), .C_IN(in_2), .SEL(in_1), .ZERO(n8bit_alu_1_zero), .out_7(out_5),
    .COUT(n8bit_alu_1_cout), .out_9(out_6), .EQ(n8bit_alu_1_eq), .LT(n8bit_alu_1_lt), .GT(n8bit_alu_1_gt),
    .ENABLE(1'b1));
  LED led_1 (.in(n8bit_alu_1_zero));
  LED led_2 (.in(n8bit_alu_1_cout));
  LED led_3 (.in(n8bit_alu_1_eq));
  LED led_4 (.in(n8bit_alu_1_gt));
  LED led_5 (.in(n8bit_alu_1_lt));
  Hex_Digit_Display hex_digit_display_1 (.value(out_5[7:4]));  // open: dp
  Hex_Digit_Display hex_digit_display_2 (.value(out_5[3:0]));  // open: dp
endmodule

module _8bit_ALU (
  input  [7:0] in_1,
  input  [7:0] in_2,
  input  C_IN,
  input  [3:0] SEL,
  input  ENABLE,
  output ZERO,
  output [7:0] out_7,
  output COUT,
  output [7:0] out_9,
  output GT,
  output EQ,
  output LT
);

  wire ADD, AND, and_3_out, CMP, DEC, INC, MUL, n8bit_adder_1_c_out, n8bit_shl_1_c_out, n8bit_shr_1_c_out,
       n8bit_substractor_1_c_out, NOT, not_1_out, not_2_out, OR, or_2_out, or_3_out, ROTL, ROTR, SHL, SHR,
       SUB, XOR;
  wire [0:0] and_2_out;
  wire [2:0] n8bit_comparator_1_gt;
  wire [7:0] and_1_out, controlled_buffer_1_out, controlled_buffer_3_out, n8bit_adder_1_out_4,
       n8bit_rotl_1_out_2, n8bit_rotr_1_out_2, n8bit_shl_1_out_3, n8bit_shr_1_out_3,
       n8bit_substractor_1_out_4, or_1_out, pull_resistor_2_node, xor_1_out;
  wire [15:0] n8bit_multiplier_1_out_3;

  _4bit_decoder u_4bit_decoder_1 (
    .ABCD(SEL), .ENABLED(ENABLE), .out_3(AND), .out_4(OR), .out_5(XOR), .out_6(NOT), .out_7(SHL),
    .out_8(SHR), .out_9(ROTL), .out_10(ROTR), .out_11(ADD), .out_12(SUB), .out_13(INC), .out_14(DEC),
    .out_15(MUL), .out_16(CMP));  // open: out_17, out_18
  Pull_Resistor #(.pull(1)) pull_resistor_1 (.node(ENABLE));
  not not_1 (not_1_out, INC);
  not not_2 (not_2_out, DEC);
  assign controlled_buffer_1_out = not_1_out ? in_2 : 8'bz;  // Controlled_Buffer controlled_buffer_1
  assign controlled_buffer_1_out = INC ? 8'h1 : 8'bz;  // Controlled_Buffer controlled_buffer_2
  assign controlled_buffer_3_out = not_2_out ? in_2 : 8'bz;  // Controlled_Buffer controlled_buffer_3
  assign controlled_buffer_3_out = DEC ? 8'h1 : 8'bz;  // Controlled_Buffer controlled_buffer_4
  assign and_1_out = in_1 & in_2;  // AND_Gate and_1, 8 bits wide
  assign or_1_out = in_1 | in_2;  // OR_Gate or_1, 8 bits wide
  assign xor_1_out = in_1 ^ in_2;  // XOR_Gate xor_1, 8 bits wide
  _8bit_shl u_8bit_shl_1 (.in_1(in_1), .c_in(C_IN), .out_3(n8bit_shl_1_out_3), .c_out(n8bit_shl_1_c_out));
  _8bit_shr u_8bit_shr_1 (.in_1(in_1), .c_in(C_IN), .out_3(n8bit_shr_1_out_3), .c_out(n8bit_shr_1_c_out));
  _8bit_rotl u_8bit_rotl_1 (.in_1(in_1), .out_2(n8bit_rotl_1_out_2));
  _8bit_rotr u_8bit_rotr_1 (.in_1(in_1), .out_2(n8bit_rotr_1_out_2));
  _8bit_adder u_8bit_adder_1 (
    .out_4(n8bit_adder_1_out_4), .in_1(C_IN), .c_out(n8bit_adder_1_c_out), .in_2(in_1),
    .in_3(controlled_buffer_1_out));
  assign out_7 = AND ? and_1_out : 8'bz;  // Controlled_Buffer controlled_buffer_5
  assign out_7 = OR ? or_1_out : 8'bz;  // Controlled_Buffer controlled_buffer_6
  assign out_7 = XOR ? xor_1_out : 8'bz;  // Controlled_Buffer controlled_buffer_7
  assign out_7 = NOT ? ~in_1 : 8'bz;  // Controlled_Inverter controlled_inverter_1
  assign out_7 = SHL ? n8bit_shl_1_out_3 : 8'bz;  // Controlled_Buffer controlled_buffer_8
  assign out_7 = SHR ? n8bit_shr_1_out_3 : 8'bz;  // Controlled_Buffer controlled_buffer_9
  assign out_7 = ROTL ? n8bit_rotl_1_out_2 : 8'bz;  // Controlled_Buffer controlled_buffer_10
  assign out_7 = ROTR ? n8bit_rotr_1_out_2 : 8'bz;  // Controlled_Buffer controlled_buffer_11
  assign COUT = or_2_out ? n8bit_adder_1_c_out : 1'bz;  // Controlled_Buffer controlled_buffer_12
  _8bit_substractor u_8bit_substractor_1 (
    .in_2(in_1), .in_3(controlled_buffer_3_out), .out_4(n8bit_substractor_1_out_4),
    .c_out(n8bit_substractor_1_c_out), .borrow(C_IN));
  assign COUT = or_3_out ? n8bit_substractor_1_c_out : 1'bz;  // Controlled_Buffer controlled_buffer_13
  _8bit_multiplier u_8bit_multiplier_1 (
    .in_1(in_1), .in_2(in_2), .out_3(n8bit_multiplier_1_out_3));  // open: out_4, HOUT
  assign COUT = SHL ? n8bit_shl_1_c_out : 1'bz;  // Controlled_Buffer controlled_buffer_14
  assign COUT = SHR ? n8bit_shr_1_c_out : 1'bz;  // Controlled_Buffer controlled_buffer_15
  assign out_7 = or_2_out ? n8bit_adder_1_out_4 : 8'bz;  // Controlled_Buffer controlled_buffer_16
  or or_2 (or_2_out, ADD, INC);
  assign out_7 = or_3_out ? n8bit_substractor_1_out_4 : 8'bz;  // Controlled_Buffer controlled_buffer_17
  or or_3 (or_3_out, SUB, DEC);
  assign {out_9, out_7} = MUL ? n8bit_multiplier_1_out_3 : 16'bz;  // Controlled_Buffer controlled_buffer_18
  Pull_Resistor #(.pull(1)) pull_resistor_2 (.node(pull_resistor_2_node));
  assign pull_resistor_2_node = out_7;  // Buffer buffer_1, 8 bits wide
  Pull_Resistor pull_resistor_3 (.node(COUT));
  and and_2 (and_2_out[0], ~ZERO, ~COUT);  // AND_Gate
  _8bit_equality_comparator u_8bit_equality_comparator_1 (.in_1({8{1'b0}}), .in_2(pull_resistor_2_node), .out_3(ZERO));
  _8bit_comparator u_8bit_comparator_1 (
    .in_1(in_1), .in_2(in_2), .EQ(n8bit_comparator_1_gt[1]), .LT(n8bit_comparator_1_gt[2]),
    .GT(n8bit_comparator_1_gt[0]));
  assign {LT, EQ, GT} = CMP ? n8bit_comparator_1_gt : 3'bz;  // Controlled_Buffer controlled_buffer_19
  assign {LT, EQ, GT} = and_3_out ? {COUT, ZERO, and_2_out[0]} : 3'bz;  // Controlled_Buffer controlled_buffer_20
  and and_3 (and_3_out, SUB, ~C_IN);  // AND_Gate

  // Other names for the same wires on the sheet: A[7:0] = in_1; B[7:0] = in_2; BORROW = C_IN; CIN = C_IN

  // Notes on the sheet:
  //   A
  //   B
  //   BORROW
  //   OUT
  //   HOUT
endmodule

module _2bit_decoder (
  input  [1:0] AB,
  input  Enabled,
  output A,
  output B,
  output C,
  output D
);

  wire and_1_out, and_2_out, and_3_out, and_4_out, not_1_out, not_2_out;

  not not_1 (not_1_out, AB[0]);
  not not_2 (not_2_out, AB[1]);
  and and_1 (and_1_out, not_1_out, not_2_out);
  and and_2 (and_2_out, AB[0], not_2_out);
  and and_3 (and_3_out, AB[1], not_1_out);
  and and_4 (and_4_out, AB[0], AB[1]);
  and and_5 (A, Enabled, and_1_out);
  and and_6 (B, Enabled, and_2_out);
  and and_7 (C, Enabled, and_3_out);
  and and_8 (D, Enabled, and_4_out);

  // Other names for the same wires on the sheet: E = Enabled
endmodule

// C
module _4bit_decoder (
  input  [3:0] ABCD,
  input  ENABLED,
  output out_3,
  output out_4,
  output out_5,
  output out_6,
  output out_7,
  output out_8,
  output out_9,
  output out_10,
  output out_11,
  output out_12,
  output out_13,
  output out_14,
  output out_15,
  output out_16,
  output out_17,
  output out_18
);

  wire n2bit_decoder_1_a, n2bit_decoder_1_b, n2bit_decoder_1_c, n2bit_decoder_1_d;

  _2bit_decoder u_2bit_decoder_1 (
    .AB({ABCD[2], ABCD[3]}), .Enabled(ENABLED), .A(n2bit_decoder_1_a), .B(n2bit_decoder_1_b),
    .C(n2bit_decoder_1_c), .D(n2bit_decoder_1_d));
  _2bit_decoder u_2bit_decoder_2 (
    .AB(ABCD[1:0]), .Enabled(n2bit_decoder_1_a), .A(out_3), .B(out_4), .C(out_5), .D(out_6));
  _2bit_decoder u_2bit_decoder_3 (
    .AB(ABCD[1:0]), .Enabled(n2bit_decoder_1_c), .A(out_7), .B(out_8), .C(out_9), .D(out_10));
  _2bit_decoder u_2bit_decoder_4 (
    .AB(ABCD[1:0]), .Enabled(n2bit_decoder_1_b), .A(out_11), .B(out_12), .C(out_13), .D(out_14));
  _2bit_decoder u_2bit_decoder_5 (
    .AB(ABCD[1:0]), .Enabled(n2bit_decoder_1_d), .A(out_15), .B(out_16), .C(out_17), .D(out_18));

  // Other names for the same wires on the sheet: A = ABCD[0]; B = ABCD[1]
endmodule

module full_adder (
  input  carry_in,
  input  A,
  input  B,
  output A_B,
  output carry_out
);

  wire and_1_out, and_2_out, xor_1_out;

  xor xor_1 (xor_1_out, A, B);
  xor xor_2 (A_B, xor_1_out, carry_in);
  and and_1 (and_1_out, carry_in, xor_1_out);
  and and_2 (and_2_out, B, A);
  xor xor_3 (carry_out, and_1_out, and_2_out);
endmodule

module _8bit_adder (
  input  in_1,
  input  [7:0] in_2,
  input  [7:0] in_3,
  output [7:0] out_4,
  output c_out
);

  wire full_adder_1_carry_out, full_adder_2_carry_out, full_adder_3_carry_out, full_adder_4_carry_out,
       full_adder_5_carry_out, full_adder_6_carry_out, full_adder_7_carry_out;

  full_adder full_adder_1 (
    .carry_in(in_1), .A(in_2[0]), .B(in_3[0]), .A_B(out_4[0]), .carry_out(full_adder_1_carry_out));
  full_adder full_adder_2 (
    .carry_in(full_adder_1_carry_out), .A(in_2[1]), .B(in_3[1]), .A_B(out_4[1]),
    .carry_out(full_adder_2_carry_out));
  full_adder full_adder_3 (
    .carry_in(full_adder_2_carry_out), .A(in_2[2]), .B(in_3[2]), .A_B(out_4[2]),
    .carry_out(full_adder_3_carry_out));
  full_adder full_adder_4 (
    .carry_in(full_adder_3_carry_out), .A(in_2[3]), .B(in_3[3]), .A_B(out_4[3]),
    .carry_out(full_adder_4_carry_out));
  full_adder full_adder_5 (
    .carry_in(full_adder_4_carry_out), .A(in_2[4]), .B(in_3[4]), .A_B(out_4[4]),
    .carry_out(full_adder_5_carry_out));
  full_adder full_adder_6 (
    .carry_in(full_adder_5_carry_out), .A(in_2[5]), .B(in_3[5]), .A_B(out_4[5]),
    .carry_out(full_adder_6_carry_out));
  full_adder full_adder_7 (
    .carry_in(full_adder_6_carry_out), .A(in_2[6]), .B(in_3[6]), .A_B(out_4[6]),
    .carry_out(full_adder_7_carry_out));
  full_adder full_adder_8 (
    .carry_in(full_adder_7_carry_out), .A(in_2[7]), .B(in_3[7]), .A_B(out_4[7]), .carry_out(c_out));

  // Notes on the sheet:
  //   A
  //   B
  //   Netřeba tunely myslím
  //   A + B
endmodule

module _8bit_substractor (
  input  borrow,
  input  [7:0] in_2,
  input  [7:0] in_3,
  output [7:0] out_4,
  output c_out
);

  wire n8bit_adder_1_c_out, not_2_out;
  wire [7:0] not_1_out;

  assign not_1_out = ~in_3;  // NOT_Gate not_1, 8 bits wide
  not not_2 (not_2_out, borrow);
  _8bit_adder u_8bit_adder_1 (
    .out_4(out_4), .in_1(not_2_out), .c_out(n8bit_adder_1_c_out), .in_2(in_2), .in_3(not_1_out));
  not not_3 (c_out, n8bit_adder_1_c_out);

  // Notes on the sheet:
  //   A
  //   B
  //   A - B
endmodule

module _4bit_multiplier (
  input  [3:0] in_1,
  input  [3:0] in_2,
  output [7:0] out_3
);

  wire adder_1_cout, adder_2_cout, adder_2_out, adder_3_cout, adder_3_out, adder_4_cout, adder_4_out,
       adder_5_cout, adder_6_cout, adder_6_out, adder_7_cout, adder_7_out, adder_8_cout, adder_8_out,
       adder_9_cout, adder_10_cout, adder_11_cout, and_2_out, and_3_out, and_4_out, and_5_out, and_6_out,
       and_7_out, and_8_out, and_9_out, and_10_out, and_11_out, and_12_out, and_13_out, and_14_out,
       and_15_out, and_16_out;

  and and_1 (out_3[0], in_1[0], in_2[0]);
  and and_2 (and_2_out, in_1[1], in_2[0]);
  and and_3 (and_3_out, in_1[2], in_2[0]);
  and and_4 (and_4_out, in_1[3], in_2[0]);
  and and_5 (and_5_out, in_1[0], in_2[1]);
  and and_6 (and_6_out, in_1[1], in_2[1]);
  and and_7 (and_7_out, in_1[2], in_2[1]);
  and and_8 (and_8_out, in_1[3], in_2[1]);
  and and_9 (and_9_out, in_1[3], in_2[2]);
  Adder #(.width(1)) adder_1 (.a(and_2_out), .b(and_5_out), .out(out_3[1]), .cin(1'b0), .cout(adder_1_cout));
  Adder #(.width(1)) adder_2 (.a(and_3_out), .b(and_6_out), .out(adder_2_out), .cin(adder_1_cout), .cout(adder_2_cout));
  Adder #(.width(1)) adder_3 (.a(and_4_out), .b(and_7_out), .out(adder_3_out), .cin(adder_2_cout), .cout(adder_3_cout));
  Adder #(.width(1)) adder_4 (.a(adder_3_cout), .b(and_8_out), .out(adder_4_out), .cin(1'b0), .cout(adder_4_cout));
  and and_10 (and_10_out, in_1[0], in_2[2]);
  and and_11 (and_11_out, in_1[1], in_2[2]);
  and and_12 (and_12_out, in_1[2], in_2[2]);
  Adder #(.width(1)) adder_5 (.a(adder_2_out), .b(and_10_out), .out(out_3[2]), .cin(1'b0), .cout(adder_5_cout));
  Adder #(.width(1)) adder_6 (
    .a(adder_3_out), .b(and_11_out), .out(adder_6_out), .cin(adder_5_cout), .cout(adder_6_cout));
  Adder #(.width(1)) adder_7 (
    .a(adder_4_out), .b(and_12_out), .out(adder_7_out), .cin(adder_6_cout), .cout(adder_7_cout));
  Adder #(.width(1)) adder_8 (
    .a(adder_4_cout), .b(and_9_out), .out(adder_8_out), .cin(adder_7_cout), .cout(adder_8_cout));
  and and_13 (and_13_out, in_1[3], in_2[3]);
  and and_14 (and_14_out, in_1[2], in_2[3]);
  and and_15 (and_15_out, in_1[0], in_2[3]);
  and and_16 (and_16_out, in_1[1], in_2[3]);
  Adder #(.width(1)) adder_9 (.a(adder_6_out), .b(and_15_out), .out(out_3[3]), .cin(1'b0), .cout(adder_9_cout));
  Adder #(.width(1)) adder_10 (
    .a(adder_7_out), .b(and_16_out), .out(out_3[4]), .cin(adder_9_cout), .cout(adder_10_cout));
  Adder #(.width(1)) adder_11 (
    .a(adder_8_out), .b(and_14_out), .out(out_3[5]), .cin(adder_10_cout), .cout(adder_11_cout));
  Adder #(.width(1)) adder_12 (.a(adder_8_cout), .b(and_13_out), .out(out_3[6]), .cin(adder_11_cout), .cout(out_3[7]));

  // Other names for the same wires on the sheet: A0 = in_1[0]; A1 = in_1[1]; A2 = in_1[2]; A3 = in_1[3]; B0 = in_2[0];
  //   B1 = in_2[1]; B2 = in_2[2]; B3 = in_2[3]

  // Notes on the sheet:
  //   /
  //   Použiti zabudované Logisim
  //   Moje sčítačka je moc veliká a má popisky xd
  //   Než abych kvůli jednomu obvodu měnil vzhled
endmodule

module _8bit_multiplier (
  input  [7:0] in_1,
  input  [7:0] in_2,
  output [15:0] out_3,
  output [7:0] out_4,
  output [7:0] HOUT
);

  wire [4:4] n8bit_adder_1_c_out;
  wire [7:0] n4bit_multiplier_2_out_3, n4bit_multiplier_3_out_3, n4bit_multiplier_4_out_3,
       n8bit_adder_1_out_4;
  wire [7:4] n4bit_multiplier_1_out_3, n8bit_adder_2_out_4;

  _4bit_multiplier u_4bit_multiplier_1 (
    .in_1(in_2[3:0]), .in_2(in_1[3:0]), .out_3({n4bit_multiplier_1_out_3, out_3[3:0]}));
  _4bit_multiplier u_4bit_multiplier_2 (.in_1(in_2[3:0]), .in_2(in_1[7:4]), .out_3(n4bit_multiplier_2_out_3));
  _4bit_multiplier u_4bit_multiplier_3 (.in_1(in_2[7:4]), .in_2(in_1[3:0]), .out_3(n4bit_multiplier_3_out_3));
  _8bit_adder u_8bit_adder_1 (
    .out_4(n8bit_adder_1_out_4), .in_1(1'b0), .c_out(n8bit_adder_1_c_out[4]),
    .in_2(n4bit_multiplier_2_out_3), .in_3(n4bit_multiplier_3_out_3));
  _8bit_adder u_8bit_adder_2 (
    .out_4({n8bit_adder_2_out_4, out_3[7:4]}), .in_1(1'b0), .in_2({4'b0000, n4bit_multiplier_1_out_3}),
    .in_3(n8bit_adder_1_out_4));  // open: c_out
  _4bit_multiplier u_4bit_multiplier_4 (.in_1(in_2[7:4]), .in_2(in_1[7:4]), .out_3(n4bit_multiplier_4_out_3));
  _8bit_adder u_8bit_adder_3 (
    .out_4(HOUT), .in_1(1'b0), .in_2({3'b000, n8bit_adder_1_c_out[4], n8bit_adder_2_out_4}),
    .in_3(n4bit_multiplier_4_out_3));  // open: c_out

  assign out_3[15:8] = HOUT;
  assign out_4 = out_3[7:0];

  // Other names for the same wires on the sheet: B4 = in_1[4]; B5 = in_1[5]; B6 = in_1[6]; B7 = in_1[7]; A4 = in_2[4];
  //   A5 = in_2[5]; A6 = in_2[6]; A7 = in_2[7]; B0 = in_1[0]; B1 = in_1[1]; B2 = in_1[2]; B3 = in_1[3]; A0 = in_2[0];
  //   A1 = in_2[1]; A2 = in_2[2]; A3 = in_2[3]

  // Notes on the sheet:
  //   ALL
  //   OUT
endmodule

module _8bit_and (
  input  [7:0] in_1,
  input  [7:0] in_2,
  output [7:0] out_3
);

  and and_1 (out_3[0], in_1[0], in_2[0]);
  and and_2 (out_3[1], in_1[1], in_2[1]);
  and and_3 (out_3[2], in_1[2], in_2[2]);
  and and_4 (out_3[3], in_1[3], in_2[3]);
  and and_5 (out_3[4], in_1[4], in_2[4]);
  and and_6 (out_3[5], in_1[5], in_1[5]);
  and and_7 (out_3[6], in_1[6], in_2[6]);
  and and_8 (out_3[7], in_1[7], in_2[7]);

  assign in_2[5] = in_1[5];

  // Notes on the sheet:
  //   A
  //   B
  //   Ukázka škálování, netřeba zde využít tunely myslím
  //   Ukázka 8 bitové AND, pro tyto 4 základní operace použiji built-in funkce Logisimu
  //   A AND B
endmodule

module _8bit_shl (
  input  [7:0] in_1,
  input  c_in,
  output [7:0] out_3,
  output c_out
);


  assign c_out = in_1[7];
  assign out_3 = {in_1[6:0], c_in};

  // Notes on the sheet:
  //   A
  //   Myslím, že takhle budou obvody srozumitelnější
  //   Šlo by to udělat v jedné komponentě samozřejmě
  //   A mensimensi 1
endmodule

module _8bit_shr (
  input  [7:0] in_1,
  input  c_in,
  output [7:0] out_3,
  output c_out
);


  assign c_out = in_1[0];
  assign out_3 = {c_in, in_1[7:1]};

  // Notes on the sheet:
  //   A
  //   A vetsivesti 1
endmodule

module _8bit_rotl (
  input  [7:0] in_1,
  output [7:0] out_2
);

  wire n8bit_shl_1_c_out;

  _8bit_shl u_8bit_shl_1 (.in_1(in_1), .c_in(n8bit_shl_1_c_out), .out_3(out_2), .c_out(n8bit_shl_1_c_out));
endmodule

module _8bit_rotr (
  input  [7:0] in_1,
  output [7:0] out_2
);

  wire n8bit_shr_1_c_out;

  _8bit_shr u_8bit_shr_1 (.in_1(in_1), .c_in(n8bit_shr_1_c_out), .out_3(out_2), .c_out(n8bit_shr_1_c_out));
endmodule

module _8bit_equality_comparator (
  input  [7:0] in_1,
  input  [7:0] in_2,
  output out_3
);

  wire xnor_1_out, xnor_2_out, xnor_3_out, xnor_4_out, xnor_5_out, xnor_6_out, xnor_7_out, xnor_8_out;

  xnor xnor_1 (xnor_1_out, in_1[0], in_2[0]);
  xnor xnor_2 (xnor_2_out, in_1[1], in_2[1]);
  xnor xnor_3 (xnor_3_out, in_1[2], in_2[2]);
  xnor xnor_4 (xnor_4_out, in_1[3], in_2[3]);
  xnor xnor_5 (xnor_5_out, in_1[4], in_2[4]);
  xnor xnor_6 (xnor_6_out, in_1[5], in_2[5]);
  xnor xnor_7 (xnor_7_out, in_1[6], in_2[6]);
  xnor xnor_8 (xnor_8_out, in_1[7], in_2[7]);
  and and_1 (out_3, xnor_1_out, xnor_2_out, xnor_3_out, xnor_4_out, xnor_5_out, xnor_6_out, xnor_7_out, xnor_8_out);
endmodule

module _8bit_comparator (
  input  [7:0] in_1,
  input  [7:0] in_2,
  output EQ,
  output LT,
  output GT
);

  wire n8bit_substractor_1_c_out, not_1_out;

  _8bit_equality_comparator u_8bit_equality_comparator_1 (.in_1(in_1), .in_2(in_2), .out_3(EQ));
  not not_1 (not_1_out, EQ);
  _8bit_substractor u_8bit_substractor_1 (
    .in_2(in_1), .in_3(in_2), .c_out(n8bit_substractor_1_c_out), .borrow(1'b0));  // open: out_4
  assign LT = not_1_out ? n8bit_substractor_1_c_out : 1'bz;  // Controlled_Buffer controlled_buffer_1
  assign GT = not_1_out ? ~n8bit_substractor_1_c_out : 1'bz;  // Controlled_Inverter controlled_inverter_1
endmodule

module TESTY (
  output [7:0] out_1,
  output [7:0] out_2,
  output [7:0] out_3,
  output [7:0] out_4,
  output [15:0] out_5,
  output [7:0] out_6,
  output [7:0] out_7,
  output [7:0] out_8,
  output [7:0] out_9,
  output [7:0] out_10,
  output [15:0] out_11,
  output [7:0] out_12,
  output [7:0] out_13,
  output [7:0] out_14,
  output [7:0] out_15,
  output [7:0] out_16
);

  wire and_2_out, and_3_out, and_4_out, comparator_1_eq, comparator_2_eq, comparator_3_eq, comparator_4_eq,
       comparator_5_eq, comparator_6_eq, comparator_7_eq, comparator_8_eq, comparator_9_eq, comparator_10_eq,
       comparator_11_eq, comparator_12_eq, comparator_13_eq, comparator_14_eq, comparator_15_eq;
  wire [7:0] adder_1_out, adder_2_out, and_1_out, multiplier_1_cout, multiplier_1_out, multiplier_2_cout,
       multiplier_2_out, shifter_1_out, shifter_2_out, shifter_3_out, shifter_4_out, shifter_5_out,
       subtractor_1_out, subtractor_2_out;
  wire [15:0] decoder_1_out0, n4bit_decoder_1_out_3;

  Adder adder_1 (.a(8'h2), .b(8'h1), .out(adder_1_out), .cin(1'b0));  // open: cout
  Subtractor subtractor_1 (.a(8'h2), .b(8'h1), .out(subtractor_1_out));  // open: bin, bout
  Subtractor subtractor_2 (.a(8'h2), .b(8'h1), .out(subtractor_2_out), .bin(1'b1));  // open: bout
  Multiplier multiplier_1 (.a(8'h2), .b(8'h1), .out(multiplier_1_out), .cin({8{1'b0}}), .cout(multiplier_1_cout));
  assign and_1_out = 8'h2 & 8'h1;  // AND_Gate and_1, 8 bits wide
  Multiplier multiplier_2 (.a(8'h39), .b(8'h6), .out(multiplier_2_out), .cin({8{1'b0}}), .cout(multiplier_2_cout));
  _4bit_decoder u_4bit_decoder_1 (
    .ABCD(4'b1001), .ENABLED(1'b1), .out_3(n4bit_decoder_1_out_3[0]), .out_4(n4bit_decoder_1_out_3[1]),
    .out_5(n4bit_decoder_1_out_3[2]), .out_6(n4bit_decoder_1_out_3[3]), .out_7(n4bit_decoder_1_out_3[4]),
    .out_8(n4bit_decoder_1_out_3[5]), .out_9(n4bit_decoder_1_out_3[6]), .out_10(n4bit_decoder_1_out_3[7]),
    .out_11(n4bit_decoder_1_out_3[8]), .out_12(n4bit_decoder_1_out_3[9]), .out_13(n4bit_decoder_1_out_3[10]),
    .out_14(n4bit_decoder_1_out_3[11]), .out_15(n4bit_decoder_1_out_3[12]),
    .out_16(n4bit_decoder_1_out_3[13]), .out_17(n4bit_decoder_1_out_3[14]), .out_18(n4bit_decoder_1_out_3[15]));
  Decoder #(.select(4)) decoder_1 (
    .out0(decoder_1_out0[0]), .out1(decoder_1_out0[1]), .out2(decoder_1_out0[2]), .out3(decoder_1_out0[3]),
    .out4(decoder_1_out0[4]), .out5(decoder_1_out0[5]), .out6(decoder_1_out0[6]), .out7(decoder_1_out0[7]),
    .out8(decoder_1_out0[8]), .out9(decoder_1_out0[9]), .out10(decoder_1_out0[10]),
    .out11(decoder_1_out0[11]), .out12(decoder_1_out0[12]), .out13(decoder_1_out0[13]),
    .out14(decoder_1_out0[14]), .out15(decoder_1_out0[15]), .sel(4'b1001), .en(1'b1));
  _8bit_adder u_8bit_adder_1 (.out_4(out_1), .in_1(1'b0), .in_2(8'h2), .in_3(8'h1));  // open: c_out
  _8bit_adder u_8bit_adder_2 (.out_4(out_2), .in_1(1'b1), .in_2(8'h2), .in_3(8'h1));  // open: c_out
  Adder adder_2 (.a(8'h2), .b(8'h1), .out(adder_2_out), .cin(1'b1));  // open: cout
  _8bit_substractor u_8bit_substractor_1 (.in_2(8'h2), .in_3(8'h1), .out_4(out_3), .borrow(1'b0));  // open: c_out
  _8bit_substractor u_8bit_substractor_2 (.in_2(8'h2), .in_3(8'h1), .out_4(out_4), .borrow(1'b1));  // open: c_out
  _8bit_multiplier u_8bit_multiplier_1 (.in_1(8'h2), .in_2(8'h1), .out_3(out_5), .out_4(out_6), .HOUT(out_7));
  _8bit_and u_8bit_and_1 (.in_1(8'h2), .in_2(8'h1), .out_3(out_8));
  _8bit_shl u_8bit_shl_1 (.in_1(8'h2), .c_in(1'b0), .out_3(out_9));  // open: c_out
  Shifter shifter_1 (.in(8'h2), .\dist (3'b001), .out(shifter_1_out));
  _8bit_shr u_8bit_shr_1 (.in_1(8'h2), .c_in(1'b0), .out_3(out_10));  // open: c_out
  Shifter #(.shift("lr")) shifter_2 (.in(8'h2), .\dist (3'b001), .out(shifter_2_out));
  _8bit_shl u_8bit_shl_2 (.in_1(8'h80), .c_in(1'b0), .out_3(out_14));  // open: c_out
  Shifter shifter_3 (.in(8'h80), .\dist (3'b001), .out(shifter_3_out));
  _8bit_rotl u_8bit_rotl_1 (.in_1(8'h80), .out_2(out_15));
  _8bit_rotr u_8bit_rotr_1 (.in_1(8'h80), .out_2(out_16));
  Comparator comparator_1 (.a(out_8), .b(and_1_out), .eq(comparator_1_eq));  // open: gt, lt
  Comparator comparator_2 (.a(out_9), .b(shifter_1_out), .eq(comparator_2_eq));  // open: gt, lt
  Comparator comparator_3 (.a(out_10), .b(shifter_2_out), .eq(comparator_3_eq));  // open: gt, lt
  _8bit_multiplier u_8bit_multiplier_2 (.in_1(8'h39), .in_2(8'h6), .out_3(out_11), .out_4(out_12), .HOUT(out_13));
  Shifter #(.shift("rl")) shifter_4 (.in(8'h80), .\dist (3'b001), .out(shifter_4_out));
  Shifter #(.shift("rr")) shifter_5 (.in(8'h80), .\dist (3'b001), .out(shifter_5_out));
  Comparator comparator_4 (.a(out_1), .b(adder_1_out), .eq(comparator_4_eq));  // open: gt, lt
  Comparator comparator_5 (.a(out_2), .b(adder_2_out), .eq(comparator_5_eq));  // open: gt, lt
  Comparator comparator_6 (.a(out_3), .b(subtractor_1_out), .eq(comparator_6_eq));  // open: gt, lt
  Comparator comparator_7 (.a(out_4), .b(subtractor_2_out), .eq(comparator_7_eq));  // open: gt, lt
  Comparator comparator_8 (.a(out_6), .b(multiplier_1_out), .eq(comparator_8_eq));  // open: gt, lt
  Comparator comparator_9 (.a(out_7), .b(multiplier_1_cout), .eq(comparator_9_eq));  // open: gt, lt
  Comparator comparator_10 (.a(out_12), .b(multiplier_2_out), .eq(comparator_10_eq));  // open: gt, lt
  Comparator comparator_11 (.a(out_13), .b(multiplier_2_cout), .eq(comparator_11_eq));  // open: gt, lt
  Comparator comparator_12 (.a(out_14), .b(shifter_3_out), .eq(comparator_12_eq));  // open: gt, lt
  Comparator comparator_13 (.a(out_15), .b(shifter_4_out), .eq(comparator_13_eq));  // open: gt, lt
  Comparator comparator_14 (.a(out_16), .b(shifter_5_out), .eq(comparator_14_eq));  // open: gt, lt
  and and_2 (and_2_out, comparator_8_eq, comparator_9_eq);
  and and_3 (and_3_out, comparator_10_eq, comparator_11_eq);
  Comparator #(.width(16)) comparator_15 (
    .a(n4bit_decoder_1_out_3), .b(decoder_1_out0), .eq(comparator_15_eq));  // open: gt, lt
  LED led_1 (.in(comparator_4_eq));
  LED led_2 (.in(comparator_5_eq));
  LED led_3 (.in(comparator_6_eq));
  LED led_4 (.in(comparator_7_eq));
  LED led_5 (.in(and_2_out));
  LED led_6 (.in(comparator_1_eq));
  LED led_7 (.in(comparator_2_eq));
  LED led_8 (.in(comparator_3_eq));
  LED led_9 (.in(and_3_out));
  LED led_10 (.in(comparator_12_eq));
  LED led_11 (.in(comparator_15_eq));
  and and_4 (and_4_out, comparator_4_eq, comparator_5_eq, comparator_6_eq, comparator_7_eq, and_2_out, comparator_1_eq, comparator_15_eq, comparator_2_eq, comparator_3_eq, and_3_out, comparator_12_eq, comparator_13_eq, comparator_14_eq);
  LED led_12 (.in(comparator_13_eq));
  LED led_13 (.in(comparator_14_eq));
  LED led_14 (.in(and_4_out));

  // Notes on the sheet:
  //   VSTUPY MOŽNO MĚNIT
  //   SROVNÁNÍ VÝSTUPU VLASTNÍCH OBVODŮ S OBVODY LOGISIMU
  //   ADD BEZ C IN
  //   ADD S C IN
  //   SUBSTRACT BEZ BORROW
  //   SUBSTRACT S BORROW
  //   MULTIPLY
  //   AND
  //   1BIT SHIFT LEFT
  //   1BIT SHIFT RIGHT
  //   MULTIPLY 2
  //   1BIT ROTATE LEFT
  //   4BIT DECODER
  //   SOUHRN TESTŮ
  //   1BIT SHIFT LEFT S OVERFLOW
  //   1BIT ROTATE RIGHT
endmodule
