// Logisim project CPU.circ as structural Verilog: 3 circuits, main circuit stepper
module stepper (
  input  in_1,
  input  in_2,
  output out_3,
  output out_4,
  output out_5,
  output out_6,
  output out_7,
  output out_8,
  output out_9,
  output out_10,
  output out_11,
  output out_12,
  output out_13
);

  wire nor_1_out, or_1_out, or_2_out, or_3_out;

  nor nor_1 (nor_1_out, or_2_out, or_3_out);
  or or_1 (or_1_out, nor_1_out, in_1);
  D_Flip_Flop d_ff_1 (.clk(in_2), .D(1'b0), .Q(out_3), .preset(or_1_out));  // open: Qn, en, reset
  D_Flip_Flop d_ff_2 (.clk(in_2), .D(out_3), .Q(out_4), .reset(or_1_out));  // open: Qn, preset, en
  or or_2 (or_2_out, out_3, out_4, out_5, out_6, out_7);
  D_Flip_Flop d_ff_3 (.clk(in_2), .D(out_4), .Q(out_5), .reset(or_1_out));  // open: Qn, preset, en
  D_Flip_Flop d_ff_4 (.clk(in_2), .D(out_5), .Q(out_6), .reset(or_1_out));  // open: Qn, preset, en
  D_Flip_Flop d_ff_5 (.clk(in_2), .D(out_6), .Q(out_7), .reset(or_1_out));  // open: Qn, preset, en
  D_Flip_Flop d_ff_6 (.clk(in_2), .D(out_7), .Q(out_8), .reset(or_1_out));  // open: Qn, preset, en
  or or_3 (or_3_out, out_8, out_9, out_10, out_11, out_12, out_13);
  D_Flip_Flop d_ff_7 (.clk(in_2), .D(out_8), .Q(out_9), .reset(or_1_out));  // open: Qn, preset, en
  D_Flip_Flop d_ff_8 (.clk(in_2), .D(out_9), .Q(out_10), .reset(or_1_out));  // open: Qn, preset, en
  D_Flip_Flop d_ff_9 (.clk(in_2), .D(out_10), .Q(out_11), .reset(or_1_out));  // open: Qn, preset, en
  D_Flip_Flop d_ff_10 (.clk(in_2), .D(out_11), .Q(out_12), .reset(or_1_out));  // open: Qn, preset, en
  D_Flip_Flop d_ff_11 (.clk(in_2), .D(out_12), .Q(out_13), .reset(or_1_out));  // open: Qn, preset, en
endmodule

module enable_set (
  input  rst,
  input  clk,
  output clk_2,
  output ena,
  output set
);

  wire or_1_out, stepper_1_out_4, stepper_1_out_6, stepper_1_out_8;

  stepper stepper_1 (
    .in_2(clk), .in_1(or_1_out), .out_3(clk_2), .out_4(stepper_1_out_4), .out_5(set),
    .out_6(stepper_1_out_6), .out_8(stepper_1_out_8));  // open: out_7, out_9, out_10, out_11, out_12, out_13
  or or_1 (or_1_out, rst, stepper_1_out_8);
  or or_2 (ena, stepper_1_out_6, stepper_1_out_4, set);
endmodule

module _8bit_cpu (
  input  in_1
);

  wire a_ena, a_set, alu_instrukce, alu_out_ena, alu_tmp_set, and_6_out, and_7_out, and_8_out, and_9_out,
       and_15_out, and_20_out, and_23_out, and_25_out, and_26_out, and_27_out, b_ena, b_set, c_ena, c_set,
       clock_1_out, d_ena, d_set, decoder_1_out0, decoder_1_out1, decoder_1_out2, decoder_2_out0,
       decoder_2_out1, ena, enable_set_1_clk_2, flag_carry, flag_zero, h_ena, h_set, hl_ena,
       imm_jmp_instrukce_inc, imm_load_instrukce, imm_load_instrukce_inc, ir_set, ira_set, jnz_instrukce_inc,
       l_ena, load_instrukce_ram, mov_reg_reg_instrukce, n8bit_alu_1_cout, n8bit_alu_1_zero, next_cycle,
       not_1_out, not_2_out, not_3_out, or_1_out, or_2_out, or_3_out, or_4_out, or_5_out, or_7_out, or_8_out,
       or_9_out, or_10_out, or_11_out, or_12_out, or_13_out, or_15_out, or_16_out, or_17_out, pc_ena, pc_inc,
       pc_set, pull_resistor_7_node, ram_set, reg_ena, reg_set, rom_ena, set, st1, st2, st3, st4, st5, st6,
       st7, stepper_1_out_10, write_instrukce_ram;
  wire [2:0] controlled_buffer_8_out, reg_ena_id, reg_set_id;
  wire [3:0] alu_sel;
  wire [5:0] buffer_2_out;
  wire [6:0] buffer_1_out;
  wire [7:0] A_q, adder_1_out, alu_out, B_q, bus, C_q, controlled_buffer_1_out, controlled_buffer_2_out,
       controlled_buffer_3_out, controlled_buffer_16_out, controlled_buffer_17_out, D_q, ir, ira,
       multiplexer_1_out, multiplexer_2_out, pc_jmp, register_1_q, register_4_q, register_5_q, rom_1_data,
       tmp_q;

  Adder adder_1 (.a(register_1_q), .b(8'h1), .out(adder_1_out));  // open: cin, cout
  Clock clock_1 (.out(clock_1_out));
  and and_1 (pc_inc, ena, or_1_out);
  and and_2 (pc_ena, ena, or_2_out);
  and and_3 (reg_ena, ena, or_3_out);
  and and_4 (hl_ena, or_4_out, ena);
  assign controlled_buffer_1_out = not_2_out ? ir : 8'bz;  // Controlled_Buffer controlled_buffer_1
  assign buffer_1_out = controlled_buffer_1_out[6:0];  // Buffer buffer_1, 7 bits wide
  assign buffer_2_out = buffer_1_out[5:0];  // Buffer buffer_2, 6 bits wide
  // Probe on multiplexer_1_out
  assign controlled_buffer_2_out = pc_inc ? adder_1_out : 8'bz;  // Controlled_Buffer controlled_buffer_2
  Multiplexer #(.width(8)) multiplexer_1 (
    .in0(controlled_buffer_2_out), .in1(pc_jmp), .out(multiplexer_1_out), .sel(not_1_out));  // open: en
  not not_1 (not_1_out, pc_inc);
  or or_1 (or_1_out, jnz_instrukce_inc, st1, imm_load_instrukce_inc);
  or or_2 (or_2_out, imm_load_instrukce_inc, st1);
  or or_3 (or_3_out, st2, st3);
  or or_4 (or_4_out, load_instrukce_ram, write_instrukce_ram);
  not not_2 (not_2_out, st1);
  enable_set enable_set_1 (.clk(clock_1_out), .clk_2(enable_set_1_clk_2), .ena(ena), .set(set), .rst(in_1));
  Pull_Resistor pull_resistor_1 (.node(controlled_buffer_1_out));
  not not_3 (not_3_out, controlled_buffer_1_out[7]);
  and and_5 (mov_reg_reg_instrukce, controlled_buffer_1_out[7], ~buffer_1_out[6]);  // AND_Gate
  // Probe on buffer_1_out[5:0]
  and and_6 (and_6_out, controlled_buffer_1_out[7], buffer_1_out[6], ~buffer_2_out[5]);  // AND_Gate
  Decoder #(.select(2), .disabled(0)) decoder_1 (
    .out0(decoder_1_out0), .out1(decoder_1_out1), .out2(decoder_1_out2), .sel(buffer_2_out[4:3]),
    .en(and_6_out));  // open: out3
  and and_7 (and_7_out, controlled_buffer_1_out[7], buffer_1_out[6], buffer_2_out[5]);
  Decoder #(.select(5), .disabled(0)) decoder_2 (
    .out0(decoder_2_out0), .out1(decoder_2_out1), .sel(buffer_2_out[4:0]), .en(and_7_out));  // open: out2, out3, out4, out5, out6, out7, out8, out9, out10, out11, out12, out13, out14, out15, out16, out17, out18, out19, out20, out21, out22, out23, out24, out25, out26, out27, out28, out29, out30, out31
  Register register_1 (.D(multiplexer_1_out), .Q(register_1_q), .clk(pc_set), .clr(in_1));  // open: en
  assign controlled_buffer_3_out = pc_ena ? register_1_q : 8'bz;  // Controlled_Buffer controlled_buffer_3
  and and_8 (and_8_out, decoder_2_out1, ~flag_zero);  // AND_Gate
  or or_5 (or_5_out, in_1, next_cycle, stepper_1_out_10);
  stepper stepper_1 (
    .in_2(enable_set_1_clk_2), .in_1(or_5_out), .out_3(st1), .out_4(st2), .out_5(st3), .out_6(st4),
    .out_7(st5), .out_8(st6), .out_9(st7), .out_10(stepper_1_out_10));  // open: out_11, out_12, out_13
  // Probe on buffer_1_out[2:0]
  // Probe on reg_set_id
  assign reg_set_id = mov_reg_reg_instrukce ? buffer_1_out[5:3] : 3'bz;  // Controlled_Buffer controlled_buffer_4
  Pull_Resistor pull_resistor_2 (.node(next_cycle));
  and and_9 (and_9_out, not_3_out, st4);
  assign reg_ena_id = mov_reg_reg_instrukce ? buffer_1_out[2:0] : 3'bz;  // Controlled_Buffer controlled_buffer_5
  and and_10 (imm_load_instrukce, and_6_out, decoder_1_out2);
  and and_11 (load_instrukce_ram, and_6_out, decoder_1_out1);
  assign reg_set_id = load_instrukce_ram ? buffer_2_out[2:0] : 3'bz;  // Controlled_Buffer controlled_buffer_6
  and and_12 (write_instrukce_ram, and_6_out, decoder_1_out0);
  or or_6 (imm_jmp_instrukce_inc, decoder_2_out0, and_8_out);
  ROM rom_1 (.addr(controlled_buffer_3_out), .data(rom_1_data), .sel(rom_ena));
  assign reg_ena_id = st2 ? controlled_buffer_8_out : 3'bz;  // Controlled_Buffer controlled_buffer_7
  assign controlled_buffer_8_out = not_3_out ? controlled_buffer_1_out[2:0] : 3'bz;  // Controlled_Buffer controlled_buffer_8
  assign alu_sel = not_3_out ? controlled_buffer_1_out[6:3] : 4'bz;  // Controlled_Buffer controlled_buffer_9
  and and_13 (alu_tmp_set, not_3_out, set, st2);
  assign reg_ena_id = write_instrukce_ram ? buffer_2_out[2:0] : 3'bz;  // Controlled_Buffer controlled_buffer_10
  assign jnz_instrukce_inc = decoder_2_out1 ? ~and_8_out : 1'bz;  // Controlled_Inverter controlled_inverter_1
  Register register_2 (.D(rom_1_data), .Q(ir), .clk(ir_set), .clr(in_1));  // open: en
  or or_7 (or_7_out, jnz_instrukce_inc, st1, imm_jmp_instrukce_inc, imm_load_instrukce_inc);
  buf or_8 (or_8_out, st1);  // OR_Gate
  or or_9 (or_9_out, load_instrukce_ram, alu_instrukce, imm_load_instrukce, mov_reg_reg_instrukce);
  buf or_10 (or_10_out, alu_instrukce);  // OR_Gate
  and and_14 (alu_instrukce, not_3_out, st3);
  and and_15 (and_15_out, mov_reg_reg_instrukce, mov_reg_reg_instrukce, st3);
  assign reg_set_id = imm_load_instrukce ? buffer_2_out[2:0] : 3'bz;  // Controlled_Buffer controlled_buffer_11
  assign pc_jmp = imm_jmp_instrukce_inc ? ira : 8'bz;  // Controlled_Buffer controlled_buffer_12
  Pull_Resistor pull_resistor_3 (.node(ir_set));
  assign reg_ena_id = alu_instrukce ? 3'b000 : 3'bz;  // Controlled_Buffer controlled_buffer_13
  assign reg_set_id = alu_instrukce ? 3'b000 : 3'bz;  // Controlled_Buffer controlled_buffer_14
  Register register_3 (.D(rom_1_data), .Q(ira), .clk(ira_set), .clr(in_1));  // open: en
  Pull_Resistor pull_resistor_4 (.node(ira_set));
  and and_16 (pc_set, set, or_7_out);
  and and_17 (ir_set, set, or_8_out);
  and and_18 (reg_set, set, or_9_out);
  and and_19 (alu_out_ena, set, or_10_out);
  or or_11 (or_11_out, imm_load_instrukce, imm_jmp_instrukce_inc);
  assign bus = imm_load_instrukce ? ira : 8'bz;  // Controlled_Buffer controlled_buffer_15
  and and_20 (and_20_out, imm_load_instrukce, imm_load_instrukce, st4);
  and and_21 (imm_load_instrukce_inc, imm_load_instrukce, imm_load_instrukce, st3);
  and and_22 (ram_set, write_instrukce_ram, set);
  Pull_Resistor pull_resistor_5 (.node(jnz_instrukce_inc));
  and and_23 (and_23_out, jnz_instrukce_inc, jnz_instrukce_inc, st3);
  and and_24 (ira_set, set, or_11_out);
  and and_25 (and_25_out, imm_jmp_instrukce_inc, imm_jmp_instrukce_inc, st4);
  Pull_Resistor pull_resistor_6 (.node(bus));
  and and_26 (and_26_out, write_instrukce_ram, write_instrukce_ram, st3);
  assign controlled_buffer_16_out = or_12_out ? register_4_q : 8'bz;  // Controlled_Buffer controlled_buffer_16
  Register register_4 (.D(bus), .Q(register_4_q), .clk(h_set));  // open: en, clr
  or or_12 (or_12_out, l_ena, hl_ena);
  // Probe on bus
  Register tmp (.D(bus), .Q(tmp_q), .clk(alu_tmp_set), .clr(in_1));  // open: en
  Pull_Resistor pull_resistor_7 (.node(pull_resistor_7_node));
  // Probe on bus
  and and_27 (and_27_out, load_instrukce_ram, load_instrukce_ram, st3);
  Register register_5 (.D(bus), .Q(register_5_q), .clk(h_set));  // open: en, clr
  // Probe on alu_sel
  Pull_Resistor pull_resistor_8 (.node(alu_sel));
  _8bit_ALU u_8bit_alu_1 (
    .in_1(bus), .in_2(tmp_q), .C_IN(pull_resistor_7_node), .SEL(alu_sel), .ZERO(n8bit_alu_1_zero),
    .out_7(alu_out), .COUT(n8bit_alu_1_cout), .ENABLE(1'b1));  // open: out_9, EQ, LT, GT
  or or_13 (or_13_out, and_9_out, and_15_out, and_27_out, and_20_out, and_26_out);
  Pull_Resistor pull_resistor_9 (.node(ram_set));
  assign controlled_buffer_17_out = or_17_out ? register_5_q : 8'bz;  // Controlled_Buffer controlled_buffer_17
  // Probe on alu_out
  Multiplexer #(.width(8)) multiplexer_2 (
    .in0(bus), .in1(alu_out), .out(multiplexer_2_out), .sel(alu_out_ena));  // open: en
  Register D (.D(bus), .Q(D_q), .clk(d_set), .clr(in_1));  // open: en
  or or_14 (next_cycle, or_13_out, or_15_out);
  or or_15 (or_15_out, and_25_out, and_23_out);
  // Probe on bus
  RAM #(.addrWidth(16), .bus("asynch")) ram_1 (
    .addr({controlled_buffer_17_out, controlled_buffer_16_out}), .data(bus), .sel(or_16_out),
    .ld(load_instrukce_ram), .clr(in_1));
  or or_16 (or_16_out, ram_set, load_instrukce_ram);
  or or_17 (or_17_out, hl_ena, h_ena);
  D_Flip_Flop d_ff_1 (.clk(alu_out_ena), .D(n8bit_alu_1_cout), .Q(flag_carry), .reset(in_1));  // open: Qn, preset, en
  D_Flip_Flop d_ff_2 (.clk(alu_out_ena), .D(n8bit_alu_1_zero), .Q(flag_zero), .reset(in_1));  // open: Qn, preset, en
  assign bus = a_ena ? A_q : 8'bz;  // Controlled_Buffer controlled_buffer_18
  Register A (.D(multiplexer_2_out), .Q(A_q), .clk(a_set), .clr(in_1));  // open: en
  Pull_Resistor pull_resistor_10 (.node(a_set));
  assign bus = b_ena ? B_q : 8'bz;  // Controlled_Buffer controlled_buffer_19
  Register B (.D(bus), .Q(B_q), .clk(b_set), .clr(in_1));  // open: en
  Pull_Resistor pull_resistor_11 (.node(b_set));
  assign bus = c_ena ? C_q : 8'bz;  // Controlled_Buffer controlled_buffer_20
  Register C (.D(bus), .Q(C_q), .clk(c_set), .clr(in_1));  // open: en
  Pull_Resistor pull_resistor_12 (.node(c_set));
  assign bus = d_ena ? D_q : 8'bz;  // Controlled_Buffer controlled_buffer_21
  Pull_Resistor pull_resistor_13 (.node(d_set));
  Pull_Resistor pull_resistor_14 (.node(a_ena));
  Pull_Resistor pull_resistor_15 (.node(b_ena));
  Pull_Resistor pull_resistor_16 (.node(c_ena));
  Pull_Resistor pull_resistor_17 (.node(d_ena));
  Pull_Resistor pull_resistor_18 (.node(load_instrukce_ram));
  Decoder #(.select(3), .disabled(0)) decoder_3 (
    .out0(a_set), .out1(b_set), .out2(c_set), .out3(d_set), .out4(h_set), .out5(h_set), .sel(reg_set_id),
    .en(reg_set));  // open: out6, out7
  // Probe on reg_set_id
  Decoder #(.select(3), .disabled(0)) decoder_4 (
    .out0(a_ena), .out1(b_ena), .out2(c_ena), .out3(d_ena), .out4(h_ena), .out5(l_ena), .sel(reg_ena_id),
    .en(reg_ena));  // open: out6, out7
  // Probe on reg_ena_id
  // also tied to GND on the sheet: {h_ena, l_ena}

  // Other names for the same wires on the sheet: l_set = h_set; load_instrukce_ram_set_id = load_instrukce_ram;
  //   ram_ena = load_instrukce_ram; rst = in_1

  // Notes on the sheet:
  //   fibonacci
  //   contents of rom_1 (hex, n*v repeats v):
  //   d0 5 d1 0 d2 1 98 82 41 8a 90 83 58 e1 6
  //   IR
  //   Ten jeden nebudu přepojovat xd
endmodule
